# Fritzing sketch attiny_rgb (saved by Fritzing 0.8.0b)
breadboards: 1

parts:
  U1 = attiny85 [package=dip]
  LED1 = RGB LED (com. cathode, rgb) [package="5 mm [THT]"]
  VCC1 = Battery

nets:
  N1: U1.Pin_2, LED1.red_anode
  N2: U1.Pin_3, LED1.blue_anode
  N3: U1.Pin_4, LED1.green_anode, VCC1.-
  N4: U1.Pin_6, LED1.common_cathode
  N5: U1.Pin_8, VCC1.+
